# Fritzing sketch Tinket Volume Knob Fritzing Sketch (saved by Fritzing 0.7.5b)
breadboards: 1

parts:
  TRINKET1 = Trinket 5V
  RE1 = Rotary Encoder [package=THT]

nets:
  N1: TRINKET1.no_name_yet#2, RE1.EncoderPinC
  N2: TRINKET1.no_name_yet#7, RE1.EncoderPinB
  N3: TRINKET1.no_name_yet#9, RE1.EncoderPinA

custom parts:
  Trinket 5V: Adafruit Trinket 5V
