# Fritzing sketch TrinketKeyboard Example Fritzing Sketch (saved by Fritzing 0.8.3b)
breadboards: 1

parts:
  TRINKET1 = Trinket 5V
  S1 = Pushbutton [package="[THT]"]
  S3 = Pushbutton [package="[THT]"]

nets:
  N1: TRINKET1.no_name_yet#2, S1.Pin_1, S1.Pin_2, S3.Pin_1, S3.Pin_2
  N2: TRINKET1.no_name_yet#7, S3.Pin_3, S3.Pin_4
  N3: TRINKET1.no_name_yet#9, S1.Pin_3, S1.Pin_4

custom parts:
  Trinket 5V: Adafruit Trinket 5V
